// Logisim project Logic3.circ as structural Verilog
module circuit3_1 (
  input  A,
  input  B,
  input  A_2,
  input  C,
  input  D,
  input  A_3,
  input  B_2,
  input  D_2,
  input  A_4,
  input  C_2,
  input  D_3,
  input  A_5,
  input  B_3,
  input  C_3,
  input  D_4
);

  wire and_1_out, and_2_out, and_3_out, and_4_out, and_5_out, not_1_out, not_2_out, not_3_out, not_4_out,
       or_1_out, or_2_out, or_3_out, or_4_out;

  and and_1 (and_1_out, A, B);
  not not_1 (not_1_out, A_2);
  not not_2 (not_2_out, A_3);
  not not_3 (not_3_out, A_4);
  not not_4 (not_4_out, D_3);
  and and_2 (and_2_out, A_5, B_3, C_3, D_4);
  and and_3 (and_3_out, not_1_out, C, D);
  and and_4 (and_4_out, not_2_out, B_2, D_2);
  and and_5 (and_5_out, not_3_out, C_2, not_4_out);
  or or_1 (or_1_out, and_1_out, and_3_out);
  or or_2 (or_2_out, or_1_out, and_4_out);
  or or_3 (or_3_out, or_2_out, and_5_out);
  // Probe on or_4_out
  or or_4 (or_4_out, or_3_out, and_2_out);
endmodule

module curcuit3_2 (
  input  A,
  input  B,
  input  C,
  input  D
);

  wire and_1_out, and_2_out, and_3_out, not_1_out, or_1_out, or_2_out;

  not not_1 (not_1_out, A);
  and and_1 (and_1_out, A, B);
  and and_2 (and_2_out, B, D);
  or or_1 (or_1_out, C, and_2_out);
  and and_3 (and_3_out, not_1_out, or_1_out);
  or or_2 (or_2_out, and_1_out, and_3_out);
  // Probe on or_2_out
endmodule
