// Logisim project circuit4.circ as structural Verilog: 4 circuits, main circuit main
module main (
  input  in_1,
  input  in_2,
  input  in_3,
  input  in_4,
  input  in_5,
  input  in_6,
  input  in_7,
  input  in_8,
  input  in_9,
  input  in_10,
  input  in_11
);

  wire n7404_ic_1_out_9, n7404_ic_2_out_9, n7404_ic_3_out_9, n7408_ic_1_out_11, n7408_ic_2_out_11,
       n7408_ic_3_out_11, n7408_ic_4_out_11, n7432_1_out_11, n7432_2_out_11, n7432_3_out_11;

  _7408_ic u_7408_ic_1 (
    .in_1(in_2), .in_3(1'b1), .in_6(in_4), .in_8(1'b0), .out_11(n7408_ic_1_out_11));  // open: in_7, in_10, in_2, in_4, in_5, in_9, out_13, out_12, out_14
  _7404_ic u_7404_ic_1 (
    .in_1(in_6), .out_9(n7404_ic_1_out_9), .in_8(1'b0), .in_2(1'b1));  // open: in_4, out_11, in_6, out_13, in_3, out_10, in_5, out_12, in_7, out_14
  // Probe on n7404_ic_1_out_9
  _7432 u_7432_1 (
    .in_1(in_8), .in_3(in_10), .out_11(n7432_1_out_11), .in_10(1'b0), .in_2(1'b1));  // open: in_6, in_7, out_13, in_4, in_5, out_12, in_8, in_9, out_14
  // Probe on n7432_1_out_11
  // Probe on n7408_ic_1_out_11
  _7404_ic u_7404_ic_2 (
    .in_1(in_5), .out_9(n7404_ic_2_out_9), .in_8(1'b0), .in_2(1'b1));  // open: in_4, out_11, in_6, out_13, in_3, out_10, in_5, out_12, in_7, out_14
  _7404_ic u_7404_ic_3 (
    .in_1(in_7), .out_9(n7404_ic_3_out_9), .in_8(1'b0), .in_2(1'b1));  // open: in_4, out_11, in_6, out_13, in_3, out_10, in_5, out_12, in_7, out_14
  _7408_ic u_7408_ic_2 (
    .in_1(in_1), .in_3(1'b1), .in_6(in_3), .in_8(1'b0), .out_11(n7408_ic_2_out_11));  // open: in_7, in_10, in_2, in_4, in_5, in_9, out_13, out_12, out_14
  _7408_ic u_7408_ic_3 (
    .in_1(n7404_ic_2_out_9), .in_3(1'b1), .in_6(n7404_ic_3_out_9), .in_8(1'b0), .out_11(n7408_ic_3_out_11));  // open: in_7, in_10, in_2, in_4, in_5, in_9, out_13, out_12, out_14
  _7408_ic u_7408_ic_4 (
    .in_1(in_9), .in_3(1'b1), .in_6(in_11), .in_8(1'b0), .out_11(n7408_ic_4_out_11));  // open: in_7, in_10, in_2, in_4, in_5, in_9, out_13, out_12, out_14
  _7432 u_7432_2 (
    .in_1(n7408_ic_2_out_11), .in_3(n7408_ic_3_out_11), .out_11(n7432_2_out_11), .in_10(1'b0), .in_2(1'b1));  // open: in_6, in_7, out_13, in_4, in_5, out_12, in_8, in_9, out_14
  _7432 u_7432_3 (
    .in_1(n7408_ic_4_out_11), .in_3(n7432_2_out_11), .out_11(n7432_3_out_11), .in_10(1'b0), .in_2(1'b1));  // open: in_6, in_7, out_13, in_4, in_5, out_12, in_8, in_9, out_14
  // Probe on n7432_3_out_11
endmodule

// 7408
module _7408_ic (
  input  in_1,
  input  in_2,
  input  in_3,
  input  in_4,
  input  in_5,
  input  in_6,
  input  in_7,
  input  in_8,
  input  in_9,
  input  in_10,
  output out_11,
  output out_12,
  output out_13,
  output out_14
);

  and and_1 (out_11, in_1, in_3);
  and and_2 (out_12, in_4, in_5);
  and and_3 (out_13, in_6, in_7);
  and and_4 (out_14, in_8, in_9);
endmodule

// 7404
module _7404_ic (
  input  in_1,
  input  in_2,
  input  in_3,
  input  in_4,
  input  in_5,
  input  in_6,
  input  in_7,
  input  in_8,
  output out_9,
  output out_10,
  output out_11,
  output out_12,
  output out_13,
  output out_14
);

  not not_1 (out_9, in_1);
  not not_2 (out_11, in_4);
  not not_3 (out_13, in_6);
  not not_4 (out_10, in_3);
  not not_5 (out_12, in_5);
  not not_6 (out_14, in_7);
endmodule

module _7432 (
  input  in_1,
  input  in_2,
  input  in_3,
  input  in_4,
  input  in_5,
  input  in_6,
  input  in_7,
  input  in_8,
  input  in_9,
  input  in_10,
  output out_11,
  output out_12,
  output out_13,
  output out_14
);

  or or_1 (out_11, in_1, in_3);
  or or_2 (out_13, in_6, in_7);
  or or_3 (out_12, in_4, in_5);
  or or_4 (out_14, in_8, in_9);
endmodule
