// Logisim project circuit5.circ as structural Verilog: 2 circuits, main circuit main
// HA
module main (
  output S,
  output C
);

  wire clock_1_out, clock_2_out;

  Clock clock_1 (.out(clock_1_out));
  Clock clock_2 (.out(clock_2_out));
  xor xor_1 (S, clock_1_out, clock_2_out);
  and and_1 (C, clock_1_out, clock_2_out);

  // Notes on the sheet:
  //   x
  //   Y
endmodule

// HA
module full (
  output s,
  output out_2
);

  wire clock_1_out, clock_2_out, clock_3_out, main_1_c, main_1_s, main_2_c;

  Clock clock_1 (.out(clock_1_out));
  Clock clock_2 (.out(clock_2_out));
  Clock clock_3 (.out(clock_3_out));
  main main_1 (.S(main_1_s), .C(main_1_c));
  main main_2 (.S(s), .C(main_2_c));
  or or_1 (out_2, main_2_c, main_1_c);

  // Notes on the sheet:
  //   x
  //   Y
  //   C_in
  //   C_out
endmodule
